# Fritzing sketch t800hk (saved by Fritzing 0.9.10b)
breadboards: 1

parts:
  IC1 = Arduino Nano (Rev3.0)
  M1 = RioRand LM2596
  V1 = DC Power [voltage=9V]
  IR1 = KY-022 Infrared Receiver Module [package="Breakout board"]
  THRUST_R = Basic Servo
  THRUST_L = Basic Servo
  TILT = Basic Servo
  TURN = Basic Servo
  LAND1 = LED - 3mm [color="White (4500K)" current=20mA package="3 mm [THT]"]
  LAND2 = LED - 3mm [color="White (4500K)" current=20mA package="3 mm [THT]"]
  R1 = Resistor [tolerance=±5% resistance=100 package="0805 [SMD]"]
  R2 = Resistor [tolerance=±5% resistance=100 package="0805 [SMD]"]
  R3 = Resistor [tolerance=±5% resistance=150 package="0805 [SMD]"]
  TAIL1 = LED - 3mm [color="Red (635nm)" current=20mA package="3 mm [THT]"]
  R4 = Resistor [tolerance=±5% resistance=100 package="0805 [SMD]"]
  TAIL2 = LED - 3mm [color="Blue (430nm)" current=20mA package="3 mm [THT]"]
  R5 = Resistor [tolerance=±5% resistance=150 package="0805 [SMD]"]
  GUN_(Purple) = LED - 3mm [color="Blue (525nm)" current=20mA package="3 mm [THT]"]
  R6 = Resistor [tolerance=±5% resistance=100 package="0805 [SMD]"]
  R7 = Resistor [tolerance=±5% resistance=100 package="0805 [SMD]"]
  SRCH2 = LED - 3mm [color="White (4500K)" current=20mA package="3 mm [THT]"]
  SRCH1 = LED - 3mm [color="White (4500K)" current=20mA package="3 mm [THT]"]
  R8 = Resistor [tolerance=±5% resistance=100 package="0805 [SMD]"]
  BLUE1 = LED - 3mm [color="Blue (430nm)" current=20mA package="3 mm [THT]"]
  R9 = Resistor [tolerance=±5% resistance=100 package="0805 [SMD]"]
  BLUE2 = LED - 3mm [color="Blue (430nm)" current=20mA package="3 mm [THT]"]
  RED1 = LED - 3mm [color="Red (635nm)" current=20mA package="3 mm [THT]"]
  R10 = Resistor [tolerance=±5% resistance=150 package="0805 [SMD]"]
  RED2 = LED - 3mm [color="Red (635nm)" current=20mA package="3 mm [THT]"]
  R11 = Resistor [tolerance=±5% resistance=150 package="0805 [SMD]"]
  DFPLAYER_PRO1 = DFRobot DFPlayer Mini [part_number=DFR0299]
  SP1 = SPEAKER [package=pcb_mount_speaker]

nets:
  GND: IC1.GND, M1.Pin_4, IR1.-, THRUST_R.gnd, THRUST_L.gnd, TILT.gnd, TURN.gnd, LAND1.cathode, LAND2.cathode, TAIL1.cathode, TAIL2.cathode, GUN_(Purple).cathode, SRCH2.cathode, SRCH1.cathode, BLUE1.cathode, BLUE2.cathode, RED1.cathode, RED2.cathode, DFPLAYER_PRO1.GND-1, DFPLAYER_PRO1.GND-2, SP1.-
  N1: IC1.D2, IR1.S
  N2: IC1.D3, DFPLAYER_PRO1.TX
  N3: IC1.D4, DFPLAYER_PRO1.RX
  N4: IC1.D5, THRUST_L.pulse
  N5: IC1.D6, THRUST_R.pulse
  N6: IC1.D7, R5.Pin_0
  N7: IC1.D8, R6.Pin_0, R7.Pin_0
  N8: IC1.D9, TILT.pulse
  N9: IC1.D10, TURN.pulse
  N10: IC1.D11/MOSI, R1.Pin_0, R2.Pin_0
  N11: IC1.D12/MISO, R3.Pin_0, R4.Pin_0
  VCC: IC1.VIN, M1.Pin_3, IR1.Vin, THRUST_R.vcc, THRUST_L.vcc, TILT.vcc, TURN.vcc, DFPLAYER_PRO1.VCC
  N12: IC1.A1, R10.Pin_0, R11.Pin_0
  N13: IC1.A0, R8.Pin_0, R9.Pin_0
  N14: M1.Pin_1, V1.V+
  N15: M1.Pin_2, V1.V-
  N16: LAND1.anode, R1.Pin_1
  N17: LAND2.anode, R2.Pin_1
  N18: R3.Pin_1, TAIL1.anode
  N19: R4.Pin_1, TAIL2.anode
  N20: R5.Pin_1, GUN_(Purple).anode
  N21: R6.Pin_1, SRCH1.anode
  N22: R7.Pin_1, SRCH2.anode
  N23: R8.Pin_1, BLUE1.anode
  N24: R9.Pin_1, BLUE2.anode
  N25: RED1.anode, R10.Pin_1
  N26: RED2.anode, R11.Pin_1
  N27: DFPLAYER_PRO1.SPK_1, SP1.+

custom parts:
  KY-022 Infrared Receiver Module: Arduino IR receiver module KY-022, based on 1838 IR Receiver/Decoder. It reacts to 38kHz infrared light.
